// Logisim project ComputerArchitectureProject.circ as structural Verilog: 5 circuits, main circuit CPU
module CPU (
  input  Reset,
  input  in_2,
  input  [7:0] in_3,
  input  [6:0] A,
  input  [6:0] B,
  output [1:0] out_6,
  output [1:0] out_7,
  output [6:0] out_8,
  output [6:0] out_9,
  output [6:0] out_10,
  output [6:0] out_11,
  output [6:0] out_12,
  output [6:0] out_13,
  output [7:0] out_14
);

  wire check, clk, demultiplexer_3_out0, demultiplexer_3_out1, demultiplexer_3_out2, demultiplexer_3_out3,
       not_1_out, odd_even, p, read, val, W, xor_1_out, xor_2_out, xor_3_out, xor_4_out, xor_5_out, xor_6_out;
  wire [1:0] code;
  wire [3:0] instr;
  wire [3:3] M_data;
  wire [6:0] multiplexer_4_out, multiplexer_5_out, R1_q, R2_q, R3_q, R4_q, Result;
  wire [7:0] C_q;

  Demultiplexer #(.width(7), .enable("false")) demultiplexer_1 (.out0(out_8), .in(A), .sel(read));  // open: out1
  Multiplexer #(.width(7), .enable("false")) multiplexer_1 (.in0(out_8), .in1(out_9), .out(out_11), .sel(val));
  Clock clock_1 (.out(clk));
  Counter C (.clr(Reset), .load(in_2), .clk(clk), .D(in_3), .Q(C_q));  // open: up, count, carry
  Demultiplexer #(.width(7), .enable("false")) demultiplexer_2 (.out0(out_9), .in(B), .sel(read));  // open: out1
  ROM #(.dataWidth(16)) M (.addr(C_q), .data({out_6, code, odd_even, W, out_7, instr, M_data[3], check, read, val}));
  Multiplexer #(.select(2), .width(7), .enable("false")) multiplexer_2 (
    .in0(out_10), .in1(Result), .in2(out_11), .out(out_12), .sel(code));  // open: in3
  Demultiplexer #(.select(2), .enable("false")) demultiplexer_3 (
    .out0(demultiplexer_3_out0), .out1(demultiplexer_3_out1), .out2(demultiplexer_3_out2),
    .out3(demultiplexer_3_out3), .in(W), .sel(out_7));
  LED Terminated (.in(M_data[3]));
  Register #(.width(7)) R1 (.D(out_12), .en(demultiplexer_3_out0), .clk(clk), .Q(R1_q));  // open: clr
  Register #(.width(7)) R2 (.D(out_12), .en(demultiplexer_3_out1), .clk(clk), .Q(R2_q));  // open: clr
  Register #(.width(7)) R3 (.D(out_12), .en(demultiplexer_3_out2), .clk(clk), .Q(R3_q));  // open: clr
  Register #(.width(7)) R4 (.D(out_12), .en(demultiplexer_3_out3), .clk(clk), .Q(R4_q));  // open: clr
  xor xor_1 (xor_1_out, out_10[0], out_10[1]);
  xor xor_2 (xor_2_out, xor_1_out, out_10[2]);
  xor xor_3 (xor_3_out, xor_2_out, out_10[3]);
  Multiplexer #(.select(2), .width(7), .enable("false")) multiplexer_3 (
    .in0(R1_q), .in1(R2_q), .in2(R3_q), .in3(R4_q), .out(out_10), .sel(out_6));
  Register Parity (.D({p, out_10}), .en(check), .clk(clk), .Q(out_14));  // open: clr
  xor xor_4 (xor_4_out, xor_3_out, out_10[4]);
  xor xor_5 (xor_5_out, xor_4_out, out_10[5]);
  Multiplexer #(.select(2), .width(7), .enable("false")) multiplexer_4 (
    .in0(R1_q), .in1(R2_q), .in2(R3_q), .in3(R4_q), .out(multiplexer_4_out), .sel(out_7));
  Multiplexer #(.select(2), .width(7), .enable("false")) multiplexer_5 (
    .in0(R1_q), .in1(R2_q), .in2(R3_q), .in3(R4_q), .out(multiplexer_5_out), .sel(out_6));
  xor xor_6 (xor_6_out, xor_5_out, out_10[6]);
  not not_1 (not_1_out, xor_6_out);
  Multiplexer #(.enable("false")) multiplexer_6 (.in0(xor_6_out), .in1(not_1_out), .out(p), .sel(odd_even));
  ALU alu_1 (.A(multiplexer_4_out), .B(multiplexer_5_out), .instruction(instr), .Result(Result), .Ignore(out_13));

  // Other names for the same wires on the sheet: Temp[6:0] = out_10; op[1:0] = code; Rd[1:0] = out_7;
  //   code[3:2] = out_6; Rs[1:0] = out_6; v[6:0] = out_11; val_in[6:0] = out_12; Value1[6:0] = out_8;
  //   Value2[6:0] = out_9

  // Notes on the sheet:
  //   contents of M (hex, n*v repeats v):
  //   2cf0 1c52 1c52 1c52 18fa 58fa
endmodule

module AU (
  input  [6:0] A,
  input  [6:0] B,
  input  f,
  output [6:0] Y
);

  wire [6:0] adder_1_out, subtractor_1_out;

  Adder #(.width(7)) adder_1 (.a(A), .b(B), .out(adder_1_out));  // open: cin, cout
  Subtractor #(.width(7)) subtractor_1 (.a(A), .b(B), .out(subtractor_1_out));  // open: bin, bout
  Multiplexer #(.width(7), .enable("false")) multiplexer_1 (
    .in0(adder_1_out), .in1(subtractor_1_out), .out(Y), .sel(f));
endmodule

module LU (
  input  [6:0] X,
  input  f,
  output [6:0] Y
);

  wire [6:0] shifter_1_out, shifter_2_out;

  Shifter #(.width(7)) shifter_1 (.in(X), .\dist (3'b001), .out(shifter_1_out));
  Shifter #(.width(7), .shift("lr")) shifter_2 (.in(X), .\dist (3'b001), .out(shifter_2_out));
  Multiplexer #(.width(7), .enable("false")) multiplexer_1 (.in0(shifter_1_out), .in1(shifter_2_out), .out(Y), .sel(f));
endmodule

module ALU (
  input  [6:0] A,
  input  [6:0] B,
  input  [3:0] instruction,
  output [6:0] Result,
  output [6:0] Ignore
);

  wire [6:0] au_1_y, lu_1_y, multiplexer_1_out;

  AU au_1 (.A(A), .B(B), .f(instruction[1]), .Y(au_1_y));
  LU lu_1 (.X(A), .f(instruction[2]), .Y(lu_1_y));
  Multiplexer #(.width(7), .enable("false")) multiplexer_1 (
    .in0(au_1_y), .in1(lu_1_y), .out(multiplexer_1_out), .sel(instruction[0]));
  Demultiplexer #(.width(7), .enable("false")) demultiplexer_1 (
    .out0(Result), .out1(Ignore), .in(multiplexer_1_out), .sel(instruction[3]));

  // Other names for the same wires on the sheet: f = instruction[0]; f1 = instruction[1]; f2 = instruction[2];
  //   x = instruction[3]
endmodule

module Registers (
  input  [7:0] value,
  input  clk,
  input  WE,
  input  y,
  input  [1:0] R,
  input  [1:0] Rd,
  output [7:0] Read,
  output [7:0] Ignore
);

  wire demultiplexer_1_out0, demultiplexer_1_out1, demultiplexer_1_out2, demultiplexer_1_out3;
  wire [7:0] multiplexer_1_out, R1_q, R2_q, R3_q, R4_q;

  Demultiplexer #(.select(2), .enable("false")) demultiplexer_1 (
    .out0(demultiplexer_1_out0), .out1(demultiplexer_1_out1), .out2(demultiplexer_1_out2),
    .out3(demultiplexer_1_out3), .in(WE), .sel(Rd));
  Register R1 (.D(value), .en(demultiplexer_1_out0), .clk(clk), .Q(R1_q));  // open: clr
  Register R2 (.D(value), .en(demultiplexer_1_out1), .clk(clk), .Q(R2_q));  // open: clr
  Register R3 (.D(value), .en(demultiplexer_1_out2), .clk(clk), .Q(R3_q));  // open: clr
  Register R4 (.D(value), .en(demultiplexer_1_out3), .clk(clk), .Q(R4_q));  // open: clr
  Multiplexer #(.select(2), .width(8), .enable("false")) multiplexer_1 (
    .in0(R1_q), .in1(R2_q), .in2(R3_q), .in3(R4_q), .out(multiplexer_1_out), .sel(R));
  Demultiplexer #(.width(8), .enable("false")) demultiplexer_2 (
    .out0(Read), .out1(Ignore), .in(multiplexer_1_out), .sel(y));

  // Other names for the same wires on the sheet: c = clk; v[7:0] = value
endmodule
